// Logisim project FIB.circ as structural Verilog: 2 circuits, main circuit main
module main (
  input  reset
);

  wire clk_out;
  wire [31:0] fib_series_1_fib, fib_series_1_n;

  Clock clk (.out(clk_out));
  Fib_series fib_series_1 (.reset(reset), .Fib(fib_series_1_fib), .n(fib_series_1_n), .clk(clk_out));
  // Probe on fib_series_1_fib
  // Probe on fib_series_1_n

  // Notes on the sheet:
  //   fib(n)  0   1   1   2   3   5   8  13
  //   n   0   1   2   3   4   5   6   7
endmodule

module Fib_series (
  input  reset,
  input  clk,
  output [31:0] Fib,
  output [31:0] n
);

  wire not_1_out;
  wire [31:0] adder_1_out, multiplexer_1_out, multiplexer_2_out, register_1_q;

  Adder #(.width(32)) adder_1 (.a(register_1_q), .b(Fib), .out(adder_1_out));  // open: cin, cout
  Multiplexer #(.width(32), .enable("false")) multiplexer_1 (
    .in0(adder_1_out), .in1(32'h1), .out(multiplexer_1_out), .sel(reset));
  // Probe on multiplexer_1_out
  Register #(.width(32), .trigger("falling")) register_1 (
    .D(multiplexer_1_out), .Q(register_1_q), .clk(clk));  // open: en, clr
  not not_1 (not_1_out, reset);
  // Probe on multiplexer_2_out
  Multiplexer #(.width(32), .enable("false")) multiplexer_2 (
    .in0(register_1_q), .in1({32{1'b0}}), .out(multiplexer_2_out), .sel(reset));
  Register #(.width(32), .trigger("falling")) register_2 (.D(multiplexer_2_out), .Q(Fib), .clk(clk));  // open: en, clr
  // Probe on Fib
  // Probe on n
  Counter #(.width(32), .max('hffffffff), .trigger("falling")) counter_1 (
    .load(reset), .D({32{1'b0}}), .count(not_1_out), .Q(n), .clk(clk));  // open: carry, clr

  // Notes on the sheet:
  //   fib(n+1)
  //   fib(n)
  //   fib(1)
  //   fib(0)
  //   This circuit computes the fibonacci series
endmodule
