// Logisim project multiplicador.circ as structural Verilog: 1 circuit, main circuit main
module main (
  input  [15:0] x,
  input  [15:0] y,
  input  empezar,
  output [31:0] out_4,
  output RDY
);

  wire clock_1_out;
  wire [15:0] factor_derecha_q, multiplexer_2_out, shifter_1_out;
  wire [31:0] adder_1_out, bit_extender_1_out, factor_izquierda_q, multiplexer_1_out, multiplexer_3_out,
       multiplexer_4_out, shifter_2_out;

  // Probe on y
  Clock clock_1 (.out(clock_1_out));
  // Probe on x
  assign bit_extender_1_out = {{16{1'b0}}, x};  // Bit_Extender bit_extender_1
  Multiplexer #(.width(32)) multiplexer_1 (
    .in0(shifter_2_out), .in1(bit_extender_1_out), .out(multiplexer_1_out), .sel(empezar));  // open: en
  Multiplexer #(.width(16)) multiplexer_2 (
    .in0(shifter_1_out), .in1(y), .out(multiplexer_2_out), .sel(empezar));  // open: en
  Register #(.width(16)) factor_derecha (
    .D(multiplexer_2_out), .Q(factor_derecha_q), .clk(clock_1_out));  // open: en, clr
  Shifter #(.width(16), .shift("lr")) shifter_1 (.in(factor_derecha_q), .\dist (4'b0001), .out(shifter_1_out));
  Shifter #(.width(32)) shifter_2 (.in(factor_izquierda_q), .\dist (5'b00001), .out(shifter_2_out));
  Register #(.width(32)) factor_izquierda (
    .D(multiplexer_1_out), .Q(factor_izquierda_q), .clk(clock_1_out));  // open: en, clr
  Adder #(.width(32)) adder_1 (.a(out_4), .b(factor_izquierda_q), .out(adder_1_out));  // open: cin, cout
  Multiplexer #(.width(32)) multiplexer_3 (
    .in0(multiplexer_4_out), .in1({32{1'b0}}), .out(multiplexer_3_out), .sel(empezar));  // open: en
  Comparator #(.width(16), .mode("unsigned")) comparator_1 (
    .a(factor_derecha_q), .b({16{1'b0}}), .eq(RDY));  // open: gt, lt
  // Probe on out_4
  Multiplexer #(.width(32)) multiplexer_4 (
    .in0(out_4), .in1(adder_1_out), .out(multiplexer_4_out), .sel(factor_derecha_q[0]));  // open: en
  Register #(.width(32)) resultado (.D(multiplexer_3_out), .Q(out_4), .clk(clock_1_out));  // open: en, clr
endmodule
